# Fritzing sketch miduino (saved by Fritzing 0.9.3b)
breadboards: 1

parts:
  Composant1 = Arduino Leonardo (Rev3b)
  S1 = Pushbutton [package="[THT]"]
  S2 = Pushbutton [package="[THT]"]
  R1 = Rotary Potentiometer (Small) [maximum_resistance=100kΩ package=THT]
  R2 = Rotary Potentiometer (Small) [maximum_resistance=100kΩ package=THT]
  J1 = Dagu DGServo 9g header (male) [package=THT]
  J2 = Dagu DGServo 9g header (male) [package=THT]
  LED1 = LED - 5mm [color="Red (633nm)" package="5 mm [THT]"]
  LED2 = LED - 5mm [color="Yellow (595nm)" package="5 mm [THT]"]
  R3 = Resistor [tolerance=±5% resistance=220 package=THT]
  R4 = Resistor [tolerance=±5% resistance=220 package=THT]
  R5 = Rotary Potentiometer (Small) [maximum_resistance=100kΩ package=THT]

nets:
  N1: Composant1.D2/SDA, S1.Pin_1, S1.Pin_2
  N2: Composant1.D3_PWM/SCL, S2.Pin_1, S2.Pin_2
  VCC: Composant1.5V, R1.leg1, R2.leg1, J1.Vcc, J2.Vcc, R5.leg1
  GND: Composant1.GND, S1.Pin_3, S1.Pin_4, S2.Pin_3, S2.Pin_4, R1.leg2, R2.leg2, J1.gnd, J2.gnd, LED1.cathode, LED2.cathode, R5.leg2
  N3: Composant1.A0, R2.wiper
  N4: Composant1.A1, R1.wiper
  N5: Composant1.A2, R5.wiper
  N6: Composant1.D10_PWM/A10, R3.Pin_1
  N7: Composant1.D11_PWM, R4.Pin_1
  N8: Composant1.D12/A11, J2.pulse
  N9: Composant1.D13_PWM, J1.pulse
  N10: LED1.anode, R3.Pin_0
  N11: LED2.anode, R4.Pin_0

notes:
  Sélecteur 16 pas
  Sélecteur 8 pistes
  Mode
  Sous-Mode
